# Fritzing sketch weather_station (saved by Fritzing 0.9.3b)
breadboards: 1

parts:
  WeMos_D1_Mini1 = WeMos D1 Mini
  RHT1 = Humidity and Temperature Sensor RHT03
  R1 = Resistor [tolerance=±5% resistance=4.7k package="0402 [SMD]"]
  Part1 = Adafruit CCS811 [part_number="Adafruit #3566"]

nets:
  3V3: WeMos_D1_Mini1.3V3, Part1.3.3V
  5V: WeMos_D1_Mini1.5V, RHT1.Vcc, R1.Pin_1
  N1: WeMos_D1_Mini1.D0, RHT1.Data-signal
  N2: WeMos_D1_Mini1.D1, Part1.SCL
  N3: WeMos_D1_Mini1.D2, Part1.SDA
  N4: WeMos_D1_Mini1.G, RHT1.GND_2, Part1.GND, Part1.!WAKE

custom parts:
  Adafruit CCS811: Breathe easy - we finally have an I2C VOC/eCO2 sensor in the Adafruit shop! Add air quality monitoring to your project and with an Adafruit CCS811 Air Quality Sensor Breakout. This sensor from AMS is a gas sensor that can detect a wide range of Volatile Organic Compounds (VOCs) and is intended for indoor air quality monitoring. When connected to your microcontroller (running our library code)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
